# Fritzing sketch NewLIRADiagram (saved by Fritzing 0.9.9b)
# 18650 Li-ion Battery: CC-BY Dr Kristofer Chan, King's College London/Remote-research.org
breadboards: 1

parts:
  A1 = u-blox NEO-6M GPS Breakout
  MCU1 = Raspberry Pi Zero
  Part1 = USB converter CP2102
  TP1 = TP4056 [chip_label=TP4056 package="DIP (Dual Inline) [THT]"]
  U1 = LIPO-2000mAh [package=lipo-2000]
  BAT1 = 18650 Li-ion Battery [package=battery-18650]  # not connected
  A2 = A7076X LTE module
  Buck_Convertor1 = Buck Convertor [part_number=LM2596 package=THT]
  A3 = mini boost module
  Q1 = NPN-Transistor [package="SOT-23 [SMD]"]
  SG1 = Buzzer 12mm [package=buzzer-12mm-ns]
  R1 = Resistor [tolerance=±5% resistance=1000 package=THT]
  R2 = Resistor [tolerance=±5% resistance=2000 package=THT]
  Mod1 = KY-016 RGB Full Color LED Module [package="Breakout board"]
  S1 = Pushbutton [package="[SMD]"]
  Power_White_LED1 = White LED
  Q2 = NPN-Transistor [package="SOT-23 [SMD]"]

nets:
  N1: A1.Pin_1, Part1.+5V, TP1.pin4, U1.+, Buck_Convertor1.Positive_Input, A3.Pin_1, Mod1.-, Power_White_LED1.White_-
  N2: A1.Pin_2, MCU1.pin_6, MCU1.pin_39, Part1.RXI, TP1.pin5, U1.-, A2.Pin_9, A2.Pin_10, A2.Pin_12, Buck_Convertor1.Negative_Input, Buck_Convertor1.Negative_Output, A3.Pin_2, R1.Pin_1, S1.Pin_1, S1.Pin_2, Q2.1
  N3: A1.Pin_3, MCU1.pin_10, MCU1.pin_12
  N4: MCU1.pin_13, Q1.0
  N5: MCU1.pin_15, Mod1.R
  N6: MCU1.pin_16, Mod1.B
  N7: MCU1.pin_18, Mod1.G
  N8: MCU1.pin_22, S1.Pin_3, S1.Pin_4
  N9: MCU1.pin_37, Q2.0
  N10: Part1.TXO, R2.Pin_0
  N11: A2.Pin_8, R2.Pin_1
  N12: A2.Pin_11, Buck_Convertor1.Positive_Output
  N13: A3.Pin_3, SG1.1
  N14: A3.Pin_4, Q1.1
  N15: Q1.2, SG1.2
  N16: Power_White_LED1.White_+, Q2.2

notes:
  USB to Micro USB (USB Cord) to Power Raspberry Pi
  Simcom A7680C-V1 with VoLTE
  QC4.0 QC3.0 LED Dual USB 5V 4.5A 22.5W Micro/Type-C USB 18650 Charging Module Temperature / Circuit Protection
  MICRO USB-TO-USB ADAPTER

custom parts:
  TP4056: A DIP stand-in part for whatever IC you want. With 6 pins on a 300mil dual inline package (DIP) footprint.
  18650 Li-ion Battery: 18650 li-ion Battery Standard 18650 battery with interactive connectors Creative Common Attribution 4.0 International (CC-BY 4.0) license. Any use of this part requires attribution of Dr Kristofer Chan, Department of Geography, King's College London. Contact kristofer.chan [at] kcl.ac.uk OR kris [at] remote-research.org for further information.
  A7076X LTE module: SIM A7672S 4G LTE TTL Modem without GNSS is a Cat-1 Module which supports wireless communication modes of LTE-TDD/LTE-FDD.
  Buck Convertor: DC to DC buck convertor
  mini boost module: mini boost module.
  KY-016 RGB Full Color LED Module: KY-016 Arduino full color 5mm RGB LED, different colors can be obtained by mixing the three primary colors.
  White LED: Testing
